// Logisim project csc258lab1_1.circ as structural Verilog: 1 circuit, main circuit main
module main (
  input  x,
  input  s,
  input  y,
  output f
);

  wire AND1_out, AND2_out, NOT1_out;

  not NOT1 (NOT1_out, s);
  and AND1 (AND1_out, x, NOT1_out);
  and AND2 (AND2_out, y, s);
  or OR1 (f, AND1_out, AND2_out);
endmodule
