// Logisim project csc258lab1_2.circ as structural Verilog: 1 circuit, main circuit main
module main (
  input  a,
  input  b,
  input  c,
  input  b2,
  input  a2,
  input  c2,
  output f,
  output f2
);

  wire AND1_out, NOT1_out, NOT2_out, NOT3_out, NOT4_out, OR1_out, OR3_out;

  not NOT1 (NOT1_out, b);
  or OR1 (OR1_out, a, b);
  not NOT3 (NOT3_out, b2);
  not NOT4 (NOT4_out, a2);
  not NOT2 (NOT2_out, OR1_out);
  and AND1 (AND1_out, NOT1_out, c);
  or OR2 (f, NOT2_out, AND1_out);
  or OR3 (OR3_out, NOT4_out, c2);
  and AND3 (f2, NOT3_out, OR3_out);
endmodule
