// Logisim project lab2.1.circ as structural Verilog: 3 circuits, main circuit main
module main (
  input  SW_0,
  input  SW_1,
  input  SW_9,
  output LEDR_9
);

  mux2to1 u (.x(SW_0), .y(SW_1), .s(SW_9), .m(LEDR_9));
endmodule

module mux2to1 (
  input  x,
  input  y,
  input  s,
  output m
);

  Multiplexer #(.enable("false")) multiplexer_1 (.in0(x), .in1(y), .out(m), .sel(s));
endmodule

module mux4to1 (
  input  u,
  input  v,
  input  s0,
  input  s1,
  input  w,
  input  x,
  output m
);

  wire mux2to1_1_m, mux2to1_3_m;

  mux2to1 mux2to1_1 (.x(u), .y(v), .s(s0), .m(mux2to1_1_m));
  mux2to1 mux2to1_3 (.x(w), .y(x), .s(s0), .m(mux2to1_3_m));
  mux2to1 mux2to1_2 (.x(mux2to1_1_m), .y(mux2to1_3_m), .s(s1), .m(m));
endmodule
