// Logisim project lab2.2.circ as structural Verilog: 8 circuits, main circuit main
module main (
  input  c3,
  input  c2,
  input  c1,
  input  c0
);

  wire segment0_1_output_1, segment1_1_f, segment2_1_f, segment3_1_f, segment4_1_f, segment5_1_f,
       segment6_1_f;

  segment6 segment6_1 (.c3(c3), .c2(c2), .c1(c1), .c0(c0), .f(segment6_1_f));
  segment0 segment0_1 (.c3(c3), .c2(c2), .c1(c1), .c0(c0), .Output_1(segment0_1_output_1));
  segment1 segment1_1 (.c3(c3), .c2(c2), .c1(c1), .c0(c0), .f(segment1_1_f));
  segment2 segment2_1 (.c3(c3), .c2(c2), .c1(c1), .c0(c0), .f(segment2_1_f));
  segment3 segment3_1 (.c3(c3), .c2(c2), .c1(c1), .c0(c0), .f(segment3_1_f));
  segment4 segment4_1 (.c3(c3), .c2(c2), .c1(c1), .c0(c0), .f(segment4_1_f));
  segment5 segment5_1 (.c3(c3), .c2(c2), .c1(c1), .c0(c0), .f(segment5_1_f));
  _7_Segment_Display #(.active("false")) L_7_Segment_Display_1 (
    .g(segment6_1_f), .f(segment5_1_f), .a(segment0_1_output_1), .b(segment1_1_f), .e(segment4_1_f),
    .d(segment3_1_f), .c(segment2_1_f));  // open: dp
endmodule

module segment1 (
  input  c3,
  input  c2,
  input  c1,
  input  c0,
  output f
);

  wire and_1_out, and_2_out, and_3_out, and_4_out, not_1_out, not_2_out, not_3_out;

  not not_1 (not_1_out, c3);
  not not_2 (not_2_out, c1);
  not not_3 (not_3_out, c0);
  and and_1 (and_1_out, c3, c2, not_2_out, not_3_out);
  and and_2 (and_2_out, not_1_out, c2, not_2_out, c0);
  and and_3 (and_3_out, c3, c1, c0);
  and and_4 (and_4_out, c2, c1, not_3_out);
  or or_1 (f, and_1_out, and_2_out, and_3_out, and_4_out);
endmodule

module segment0 (
  input  c3,
  input  c2,
  input  c1,
  input  c0,
  output Output_1
);

  wire and_1_out, and_2_out, and_3_out, and_4_out, not_1_out, not_2_out, not_3_out, not_4_out;

  not not_1 (not_1_out, c3);
  not not_2 (not_2_out, c2);
  not not_3 (not_3_out, c1);
  not not_4 (not_4_out, c0);
  and and_1 (and_1_out, not_1_out, not_2_out, not_3_out, c0);
  and and_2 (and_2_out, not_1_out, c2, not_3_out, not_4_out);
  and and_3 (and_3_out, c3, c2, not_3_out, c0);
  and and_4 (and_4_out, c3, not_2_out, c1, c0);
  or or_1 (Output_1, and_1_out, and_2_out, and_3_out, and_4_out);
endmodule

module segment2 (
  input  c3,
  input  c2,
  input  c1,
  input  c0,
  output f
);

  wire and_1_out, and_2_out, and_3_out, not_1_out, not_2_out, not_3_out, not_4_out;

  not not_1 (not_1_out, c3);
  not not_2 (not_2_out, c2);
  not not_3 (not_3_out, c1);
  not not_4 (not_4_out, c0);
  and and_1 (and_1_out, c3, c2, not_3_out, not_4_out);
  and and_2 (and_2_out, c3, c2, c1);
  and and_3 (and_3_out, not_1_out, not_2_out, c1, not_4_out);
  or or_1 (f, and_1_out, and_2_out, and_3_out);
endmodule

module segment3 (
  input  c3,
  input  c2,
  input  c1,
  input  c0,
  output f
);

  wire and_1_out, and_2_out, and_3_out, and_4_out, not_1_out, not_2_out, not_3_out, not_4_out;

  not not_1 (not_1_out, c3);
  not not_2 (not_2_out, c2);
  not not_3 (not_3_out, c1);
  not not_4 (not_4_out, c0);
  and and_1 (and_1_out, not_1_out, c2, not_3_out, not_4_out);
  and and_2 (and_2_out, not_1_out, not_2_out, not_3_out, c0);
  and and_3 (and_3_out, c2, c1, c0);
  and and_4 (and_4_out, c3, not_2_out, c1, not_4_out);
  or or_1 (f, and_1_out, and_2_out, and_3_out, and_4_out);
endmodule

module segment4 (
  input  c3,
  input  c2,
  input  c1,
  input  c0,
  output f
);

  wire and_1_out, and_2_out, and_3_out, not_1_out, not_2_out, not_3_out, not_4_out;

  not not_1 (not_1_out, c3);
  not not_2 (not_2_out, c2);
  not not_3 (not_3_out, c1);
  not not_4 (not_4_out, c0);
  and and_1 (and_1_out, not_1_out, c0);
  and and_2 (and_2_out, not_1_out, c2, not_3_out, not_4_out);
  and and_3 (and_3_out, c3, not_2_out, not_3_out, c0);
  or or_1 (f, and_1_out, and_2_out, and_3_out);
endmodule

module segment5 (
  input  c3,
  input  c2,
  input  c1,
  input  c0,
  output f
);

  wire and_1_out, and_2_out, and_3_out, and_4_out, not_1_out, not_2_out, not_3_out, not_4_out;

  not not_1 (not_1_out, c3);
  not not_2 (not_2_out, c2);
  not not_3 (not_3_out, c1);
  not not_4 (not_4_out, c0);
  and and_1 (and_1_out, not_1_out, not_2_out, not_3_out, c0);
  and and_2 (and_2_out, c3, c2, not_3_out, c0);
  and and_3 (and_3_out, not_1_out, c1, c0);
  and and_4 (and_4_out, not_1_out, not_2_out, c1, not_4_out);
  or or_1 (f, and_1_out, and_2_out, and_3_out, and_4_out);
endmodule

module segment6 (
  input  c3,
  input  c2,
  input  c1,
  input  c0,
  output f
);

  wire and_1_out, and_2_out, and_3_out, not_1_out, not_2_out, not_3_out, not_4_out;

  not not_1 (not_1_out, c3);
  not not_2 (not_2_out, c2);
  not not_3 (not_3_out, c1);
  not not_4 (not_4_out, c0);
  and and_1 (and_1_out, c3, c2, not_3_out, not_4_out);
  and and_2 (and_2_out, not_1_out, not_2_out, not_3_out);
  and and_3 (and_3_out, not_1_out, c2, c1, c0);
  or or_1 (f, and_1_out, and_2_out, and_3_out);
endmodule
