// Logisim project lab3.1.circ as structural Verilog: 1 circuit, main circuit main
module main (
  input  [9:0] SW_0,
  output LEDR0
);

  Multiplexer #(.enable("false"), .select(3)) multiplexer_1 (
    .in0(SW_0[0]), .in1(SW_0[1]), .in2(SW_0[2]), .in3(SW_0[3]), .in4(SW_0[4]), .in5(SW_0[5]), .in6(SW_0[6]),
    .in7(1'b0), .out(LEDR0), .sel(SW_0[9:7]));
endmodule
