// Logisim project lab5.circ as structural Verilog
module eightBitCounter (
  input  Enable,
  input  Clock,
  input  Clear_b,
  output Q0,
  output Q2,
  output Q7,
  output Q1,
  output Q3,
  output Q4,
  output Q5,
  output Q6,
  output [7:0] output1
);

  wire and_1_out, and_2_out, and_3_out, and_4_out, and_5_out, and_6_out, and_7_out,
       hex_decoder_submain_1_out_5, hex_decoder_submain_1_out_6, hex_decoder_submain_1_out_7,
       hex_decoder_submain_1_out_8, hex_decoder_submain_1_out_9, hex_decoder_submain_1_out_10,
       hex_decoder_submain_1_out_11, hex_decoder_submain_2_out_5, hex_decoder_submain_2_out_6,
       hex_decoder_submain_2_out_7, hex_decoder_submain_2_out_8, hex_decoder_submain_2_out_9,
       hex_decoder_submain_2_out_10, hex_decoder_submain_2_out_11;

  T_Flip_Flop t_ff_1 (.T(Enable), .clk(Clock), .Q(output1[0]), .reset(Clear_b));  // open: Qn, preset
  and and_1 (and_1_out, Enable, output1[0]);
  T_Flip_Flop t_ff_2 (.T(and_1_out), .clk(Clock), .Q(output1[1]), .reset(Clear_b));  // open: Qn, preset
  and and_2 (and_2_out, and_1_out, output1[1]);
  T_Flip_Flop t_ff_3 (.T(and_2_out), .clk(Clock), .Q(output1[2]), .reset(Clear_b));  // open: Qn, preset
  and and_3 (and_3_out, and_2_out, output1[2]);
  T_Flip_Flop t_ff_4 (.T(and_3_out), .clk(Clock), .Q(output1[3]), .reset(Clear_b));  // open: Qn, preset
  HEX_decoder_submain hex_decoder_submain_1 (
    .c3(output1[3]), .c2(output1[2]), .c1(output1[1]), .c0(output1[0]), .out_5(hex_decoder_submain_1_out_5),
    .out_6(hex_decoder_submain_1_out_6), .out_7(hex_decoder_submain_1_out_7),
    .out_8(hex_decoder_submain_1_out_8), .out_9(hex_decoder_submain_1_out_9),
    .out_10(hex_decoder_submain_1_out_10), .out_11(hex_decoder_submain_1_out_11));
  HEX_decoder_submain hex_decoder_submain_2 (
    .c3(output1[7]), .c2(output1[6]), .c1(output1[5]), .c0(output1[4]), .out_5(hex_decoder_submain_2_out_5),
    .out_6(hex_decoder_submain_2_out_6), .out_7(hex_decoder_submain_2_out_7),
    .out_8(hex_decoder_submain_2_out_8), .out_9(hex_decoder_submain_2_out_9),
    .out_10(hex_decoder_submain_2_out_10), .out_11(hex_decoder_submain_2_out_11));
  and and_4 (and_4_out, and_3_out, output1[3]);
  T_Flip_Flop t_ff_5 (.T(and_4_out), .clk(Clock), .Q(output1[4]), .reset(Clear_b));  // open: Qn, preset
  and and_5 (and_5_out, and_4_out, output1[4]);
  T_Flip_Flop t_ff_6 (.T(and_5_out), .clk(Clock), .Q(output1[5]), .reset(Clear_b));  // open: Qn, preset
  _7_Segment_Display #(.active("false")) u_7_segment_display_1 (
    .g(hex_decoder_submain_2_out_11), .f(hex_decoder_submain_2_out_10), .a(hex_decoder_submain_2_out_5),
    .b(hex_decoder_submain_2_out_6), .e(hex_decoder_submain_2_out_9), .d(hex_decoder_submain_2_out_8),
    .c(hex_decoder_submain_2_out_7));  // open: dp
  _7_Segment_Display #(.active("false")) u_7_segment_display_2 (
    .g(hex_decoder_submain_1_out_11), .f(hex_decoder_submain_1_out_10), .a(hex_decoder_submain_1_out_5),
    .b(hex_decoder_submain_1_out_6), .e(hex_decoder_submain_1_out_9), .d(hex_decoder_submain_1_out_8),
    .c(hex_decoder_submain_1_out_7));  // open: dp
  and and_6 (and_6_out, and_5_out, output1[5]);
  T_Flip_Flop t_ff_7 (.T(and_6_out), .clk(Clock), .Q(output1[6]), .reset(Clear_b));  // open: Qn, preset
  and and_7 (and_7_out, and_6_out, output1[6]);
  T_Flip_Flop t_ff_8 (.T(and_7_out), .clk(Clock), .Q(output1[7]), .reset(Clear_b));  // open: Qn, preset

  assign Q0 = output1[0];
  assign Q1 = output1[1];
  assign Q2 = output1[2];
  assign Q3 = output1[3];
  assign Q4 = output1[4];
  assign Q5 = output1[5];
  assign Q6 = output1[6];
  assign Q7 = output1[7];
endmodule

module part2main (
  input  SW2,
  input  [1:0] SW1_0
);

  wire clk_out, fourbitcounter_1_q0, fourbitcounter_1_q1, fourbitcounter_1_q2, fourbitcounter_1_q3,
       hex_decoder_submain_1_out_5, hex_decoder_submain_1_out_6, hex_decoder_submain_1_out_7,
       hex_decoder_submain_1_out_8, hex_decoder_submain_1_out_9, hex_decoder_submain_1_out_10,
       hex_decoder_submain_1_out_11, multiplexer_1_out, ratedivider_1_newclock;

  Clock clk (.out(clk_out));
  Multiplexer #(.enable("false"), .select(2)) multiplexer_1 (
    .in0(1'b1), .in1(ratedivider_1_newclock), .in2(ratedivider_1_newclock), .in3(ratedivider_1_newclock),
    .out(multiplexer_1_out), .sel(SW1_0));
  rateDivider ratedivider_1 (.clock(clk_out), .reset(SW2), .SW(SW1_0), .newClock(ratedivider_1_newclock));
  fourbitCounter fourbitcounter_1 (
    .Enable(multiplexer_1_out), .Clock(clk_out), .Clear_b(SW2), .Q0(fourbitcounter_1_q0),
    .Q1(fourbitcounter_1_q1), .Q2(fourbitcounter_1_q2), .Q3(fourbitcounter_1_q3));
  HEX_decoder_submain hex_decoder_submain_1 (
    .c3(fourbitcounter_1_q3), .c2(fourbitcounter_1_q2), .c1(fourbitcounter_1_q1), .c0(fourbitcounter_1_q0),
    .out_5(hex_decoder_submain_1_out_5), .out_6(hex_decoder_submain_1_out_6),
    .out_7(hex_decoder_submain_1_out_7), .out_8(hex_decoder_submain_1_out_8),
    .out_9(hex_decoder_submain_1_out_9), .out_10(hex_decoder_submain_1_out_10),
    .out_11(hex_decoder_submain_1_out_11));
  _7_Segment_Display #(.active("false")) HEX0 (
    .g(hex_decoder_submain_1_out_11), .f(hex_decoder_submain_1_out_10), .a(hex_decoder_submain_1_out_5),
    .b(hex_decoder_submain_1_out_6), .e(hex_decoder_submain_1_out_9), .d(hex_decoder_submain_1_out_8),
    .c(hex_decoder_submain_1_out_7));  // open: dp
endmodule

module rateDivider (
  input  clock,
  input  reset,
  input  [1:0] SW,
  output newClock
);

  wire divideby16_1_counter_out, divideby32_1_counter_out, divideby64_1_counter_out;

  divideBy16 divideby16_1 (.clear(reset), .clock(clock), .counter_out(divideby16_1_counter_out));
  divideBy32 divideby32_1 (.clear(reset), .clock(clock), .counter_out(divideby32_1_counter_out));
  divideBy64 divideby64_1 (.clear(reset), .clock(clock), .counter_out(divideby64_1_counter_out));
  Multiplexer #(.enable("false"), .select(2)) multiplexer_1 (
    .in0(clock), .in1(divideby16_1_counter_out), .in2(divideby32_1_counter_out),
    .in3(divideby64_1_counter_out), .out(newClock), .sel(SW));
endmodule

module divideBy8 (
  input  clear,
  input  clock,
  output counter_out
);

  wire not_1_out, or_1_out;
  wire [2:0] counter_1_q;

  not not_1 (not_1_out, 1'b1);
  Counter #(.max('h7), .width(3)) counter_1 (
    .clr(clear), .load(or_1_out), .up(1'b1), .clk(clock), .D(3'b000), .Q(counter_1_q));  // open: count, carry
  or or_1 (or_1_out, counter_out, not_1_out);
  and and_1 (counter_out, counter_1_q[0], counter_1_q[1], counter_1_q[2]);
endmodule

module divideBy16 (
  input  clear,
  input  clock,
  output counter_out
);

  wire not_1_out, or_1_out;
  wire [3:0] counter_1_q;

  not not_1 (not_1_out, 1'b1);
  Counter #(.max('hf), .width(4)) counter_1 (
    .clr(clear), .load(or_1_out), .up(1'b1), .clk(clock), .D(4'b0000), .Q(counter_1_q));  // open: count, carry
  or or_1 (or_1_out, counter_out, not_1_out);
  and and_1 (counter_out, counter_1_q[0], counter_1_q[1], counter_1_q[2], counter_1_q[3]);
endmodule

module divideBy32 (
  input  clear,
  input  clock,
  output counter_out
);

  wire not_1_out, or_1_out;
  wire [4:0] counter_1_q;

  not not_1 (not_1_out, 1'b1);
  Counter #(.max('h1f), .width(5)) counter_1 (
    .clr(clear), .load(or_1_out), .up(1'b1), .clk(clock), .D({5{1'b0}}), .Q(counter_1_q));  // open: count, carry
  or or_1 (or_1_out, counter_out, not_1_out);
  and and_1 (counter_out, counter_1_q[0], counter_1_q[1], counter_1_q[2], counter_1_q[3], counter_1_q[4]);
endmodule

module divideBy64 (
  input  clear,
  input  clock,
  output counter_out
);

  wire not_1_out, or_1_out;
  wire [5:0] counter_1_q;

  not not_1 (not_1_out, 1'b1);
  Counter #(.max('h3f), .width(6)) counter_1 (
    .clr(clear), .load(or_1_out), .up(1'b1), .clk(clock), .D({6{1'b0}}), .Q(counter_1_q));  // open: count, carry
  or or_1 (or_1_out, counter_out, not_1_out);
  and and_1 (counter_out, counter_1_q[0], counter_1_q[1], counter_1_q[2], counter_1_q[3], counter_1_q[4], counter_1_q[5]);
endmodule

module part3main (
  input  [2:0] SW2_0,
  input  KEY_1,
  input  KEY_0,
  output [13:0] LEDR_0
);

  wire clock_1_out, divideby8_1_counter_out;
  wire [13:0] lut_1_output_lut;

  Clock clock_1 (.out(clock_1_out));
  LUT lut_1 (.in_1(SW2_0), .Output_LUT(lut_1_output_lut));
  divideBy8 divideby8_1 (.clear(KEY_0), .clock(clock_1_out), .counter_out(divideby8_1_counter_out));
  BitShifter14 bitshifter14_1 (
    .LoadVal(lut_1_output_lut), .shiftRight(1'b1), .load_n(KEY_1), .clk(divideby8_1_counter_out),
    .reset(KEY_0), .ASR(1'b0), .out_7(LEDR_0));
  LED led_1 (.in(LEDR_0[0]));
endmodule

module LUT (
  input  [2:0] in_1,
  output [13:0] Output_LUT
);

  Multiplexer #(.enable("false"), .select(3), .width(14)) multiplexer_1 (
    .in0(14'h2a00), .in1(14'h3800), .in2(14'h2b80), .in3(14'h2ae0), .in4(14'h2ee0), .in5(14'h3ab8),
    .in6(14'h3aee), .in7(14'h3ba8), .out(Output_LUT), .sel(in_1));
endmodule

module BitShifter14 (
  input  [13:0] LoadVal,
  input  shiftRight,
  input  load_n,
  input  clk,
  input  reset,
  input  ASR,
  output [13:0] out_7
);

  wire mux2to1_1_m;

  mux2to1 mux2to1_1 (.x(1'b0), .y(ASR), .s(out_7[13]), .m(mux2to1_1_m));
  shifterBit SB0 (
    .load_val(LoadVal[0]), .in1(out_7[1]), .shift(shiftRight), .load_n(load_n), .clk(clk), .reset(reset),
    .Q(out_7[0]));
  shifterBit SB1 (
    .load_val(LoadVal[1]), .in1(out_7[2]), .shift(shiftRight), .load_n(load_n), .clk(clk), .reset(reset),
    .Q(out_7[1]));
  shifterBit SB2 (
    .load_val(LoadVal[2]), .in1(out_7[3]), .shift(shiftRight), .load_n(load_n), .clk(clk), .reset(reset),
    .Q(out_7[2]));
  shifterBit SB3 (
    .load_val(LoadVal[3]), .in1(out_7[4]), .shift(shiftRight), .load_n(load_n), .clk(clk), .reset(reset),
    .Q(out_7[3]));
  shifterBit SB4 (
    .load_val(LoadVal[4]), .in1(out_7[5]), .shift(shiftRight), .load_n(load_n), .clk(clk), .reset(reset),
    .Q(out_7[4]));
  shifterBit SB5 (
    .load_val(LoadVal[5]), .in1(out_7[6]), .shift(shiftRight), .load_n(load_n), .clk(clk), .reset(reset),
    .Q(out_7[5]));
  shifterBit SB6 (
    .load_val(LoadVal[6]), .in1(out_7[7]), .shift(shiftRight), .load_n(load_n), .clk(clk), .reset(reset),
    .Q(out_7[6]));
  shifterBit SB7 (
    .load_val(LoadVal[7]), .in1(out_7[8]), .shift(shiftRight), .load_n(load_n), .clk(clk), .reset(reset),
    .Q(out_7[7]));
  shifterBit SB8 (
    .load_val(LoadVal[8]), .in1(out_7[9]), .shift(shiftRight), .load_n(load_n), .clk(clk), .reset(reset),
    .Q(out_7[8]));
  shifterBit SB9 (
    .load_val(LoadVal[9]), .in1(out_7[10]), .shift(shiftRight), .load_n(load_n), .clk(clk), .reset(reset),
    .Q(out_7[9]));
  shifterBit SB10 (
    .load_val(LoadVal[10]), .in1(out_7[11]), .shift(shiftRight), .load_n(load_n), .clk(clk), .reset(reset),
    .Q(out_7[10]));
  shifterBit SB11 (
    .load_val(LoadVal[11]), .in1(out_7[12]), .shift(shiftRight), .load_n(load_n), .clk(clk), .reset(reset),
    .Q(out_7[11]));
  shifterBit SB12 (
    .load_val(LoadVal[12]), .in1(out_7[13]), .shift(shiftRight), .load_n(load_n), .clk(clk), .reset(reset),
    .Q(out_7[12]));
  shifterBit SB13 (
    .load_val(LoadVal[13]), .in1(mux2to1_1_m), .shift(shiftRight), .load_n(load_n), .clk(clk), .reset(reset),
    .Q(out_7[13]));
endmodule

module segment1 (
  input  c3,
  input  c2,
  input  c1,
  input  c0,
  output f
);

  wire and_1_out, and_2_out, and_3_out, and_4_out, not_1_out, not_2_out, not_3_out;

  not not_1 (not_1_out, c3);
  not not_2 (not_2_out, c1);
  not not_3 (not_3_out, c0);
  and and_1 (and_1_out, c3, c2, not_2_out, not_3_out);
  and and_2 (and_2_out, not_1_out, c2, not_2_out, c0);
  and and_3 (and_3_out, c3, c1, c0);
  and and_4 (and_4_out, c2, c1, not_3_out);
  or or_1 (f, and_1_out, and_2_out, and_3_out, and_4_out);
endmodule

module segment0 (
  input  c3,
  input  c2,
  input  c1,
  input  c0,
  output Output_1
);

  wire and_1_out, and_2_out, and_3_out, and_4_out, not_1_out, not_2_out, not_3_out, not_4_out;

  not not_1 (not_1_out, c3);
  not not_2 (not_2_out, c2);
  not not_3 (not_3_out, c1);
  not not_4 (not_4_out, c0);
  and and_1 (and_1_out, not_1_out, not_2_out, not_3_out, c0);
  and and_2 (and_2_out, not_1_out, c2, not_3_out, not_4_out);
  and and_3 (and_3_out, c3, c2, not_3_out, c0);
  and and_4 (and_4_out, c3, not_2_out, c1, c0);
  or or_1 (Output_1, and_1_out, and_2_out, and_3_out, and_4_out);
endmodule

module segment2 (
  input  c3,
  input  c2,
  input  c1,
  input  c0,
  output f
);

  wire and_1_out, and_2_out, and_3_out, not_1_out, not_2_out, not_3_out, not_4_out;

  not not_1 (not_1_out, c3);
  not not_2 (not_2_out, c2);
  not not_3 (not_3_out, c1);
  not not_4 (not_4_out, c0);
  and and_1 (and_1_out, c3, c2, not_3_out, not_4_out);
  and and_2 (and_2_out, c3, c2, c1);
  and and_3 (and_3_out, not_1_out, not_2_out, c1, not_4_out);
  or or_1 (f, and_1_out, and_2_out, and_3_out);
endmodule

module segment3 (
  input  c3,
  input  c2,
  input  c1,
  input  c0,
  output f
);

  wire and_1_out, and_2_out, and_3_out, and_4_out, not_1_out, not_2_out, not_3_out, not_4_out;

  not not_1 (not_1_out, c3);
  not not_2 (not_2_out, c2);
  not not_3 (not_3_out, c1);
  not not_4 (not_4_out, c0);
  and and_1 (and_1_out, not_1_out, c2, not_3_out, not_4_out);
  and and_2 (and_2_out, not_1_out, not_2_out, not_3_out, c0);
  and and_3 (and_3_out, c2, c1, c0);
  and and_4 (and_4_out, c3, not_2_out, c1, not_4_out);
  or or_1 (f, and_1_out, and_2_out, and_3_out, and_4_out);
endmodule

module segment4 (
  input  c3,
  input  c2,
  input  c1,
  input  c0,
  output f
);

  wire and_1_out, and_2_out, and_3_out, not_1_out, not_2_out, not_3_out, not_4_out;

  not not_1 (not_1_out, c3);
  not not_2 (not_2_out, c2);
  not not_3 (not_3_out, c1);
  not not_4 (not_4_out, c0);
  and and_1 (and_1_out, not_1_out, c0);
  and and_2 (and_2_out, not_1_out, c2, not_3_out, not_4_out);
  and and_3 (and_3_out, c3, not_2_out, not_3_out, c0);
  or or_1 (f, and_1_out, and_2_out, and_3_out);
endmodule

module segment5 (
  input  c3,
  input  c2,
  input  c1,
  input  c0,
  output f
);

  wire and_1_out, and_2_out, and_3_out, and_4_out, not_1_out, not_2_out, not_3_out, not_4_out;

  not not_1 (not_1_out, c3);
  not not_2 (not_2_out, c2);
  not not_3 (not_3_out, c1);
  not not_4 (not_4_out, c0);
  and and_1 (and_1_out, not_1_out, not_2_out, not_3_out, c0);
  and and_2 (and_2_out, c3, c2, not_3_out, c0);
  and and_3 (and_3_out, not_1_out, c1, c0);
  and and_4 (and_4_out, not_1_out, not_2_out, c1, not_4_out);
  or or_1 (f, and_1_out, and_2_out, and_3_out, and_4_out);
endmodule

module segment6 (
  input  c3,
  input  c2,
  input  c1,
  input  c0,
  output f
);

  wire and_1_out, and_2_out, and_3_out, not_1_out, not_2_out, not_3_out, not_4_out;

  not not_1 (not_1_out, c3);
  not not_2 (not_2_out, c2);
  not not_3 (not_3_out, c1);
  not not_4 (not_4_out, c0);
  and and_1 (and_1_out, c3, c2, not_3_out, not_4_out);
  and and_2 (and_2_out, not_1_out, not_2_out, not_3_out);
  and and_3 (and_3_out, not_1_out, c2, c1, c0);
  or or_1 (f, and_1_out, and_2_out, and_3_out);
endmodule

module HEX_decoder (
  input  c3,
  input  c2,
  input  c1,
  input  c0
);

  wire hex_decoder_submain_1_out_5, hex_decoder_submain_1_out_6, hex_decoder_submain_1_out_7,
       hex_decoder_submain_1_out_8, hex_decoder_submain_1_out_9, hex_decoder_submain_1_out_10,
       hex_decoder_submain_1_out_11;

  HEX_decoder_submain hex_decoder_submain_1 (
    .c3(c3), .c2(c2), .c1(c1), .c0(c0), .out_5(hex_decoder_submain_1_out_5),
    .out_6(hex_decoder_submain_1_out_6), .out_7(hex_decoder_submain_1_out_7),
    .out_8(hex_decoder_submain_1_out_8), .out_9(hex_decoder_submain_1_out_9),
    .out_10(hex_decoder_submain_1_out_10), .out_11(hex_decoder_submain_1_out_11));
  _7_Segment_Display #(.active("false")) L_7_Segment_Display_1 (
    .g(hex_decoder_submain_1_out_11), .f(hex_decoder_submain_1_out_10), .a(hex_decoder_submain_1_out_5),
    .b(hex_decoder_submain_1_out_6), .e(hex_decoder_submain_1_out_9), .d(hex_decoder_submain_1_out_8),
    .c(hex_decoder_submain_1_out_7));  // open: dp
endmodule

module HEX_decoder_submain (
  input  c3,
  input  c2,
  input  c1,
  input  c0,
  output out_5,
  output out_6,
  output out_7,
  output out_8,
  output out_9,
  output out_10,
  output out_11
);

  segment6 segment6_1 (.c3(c3), .c2(c2), .c1(c1), .c0(c0), .f(out_11));
  segment0 segment0_1 (.c3(c3), .c2(c2), .c1(c1), .c0(c0), .Output_1(out_5));
  segment1 segment1_1 (.c3(c3), .c2(c2), .c1(c1), .c0(c0), .f(out_6));
  segment2 segment2_1 (.c3(c3), .c2(c2), .c1(c1), .c0(c0), .f(out_7));
  segment3 segment3_1 (.c3(c3), .c2(c2), .c1(c1), .c0(c0), .f(out_8));
  segment4 segment4_1 (.c3(c3), .c2(c2), .c1(c1), .c0(c0), .f(out_9));
  segment5 segment5_1 (.c3(c3), .c2(c2), .c1(c1), .c0(c0), .f(out_10));
endmodule

module fourbitCounter (
  input  Enable,
  input  Clock,
  input  Clear_b,
  output Q0,
  output Q1,
  output Q2,
  output Q3
);

  wire and_1_out, and_2_out, and_3_out;

  T_Flip_Flop t_ff_1 (.T(Enable), .clk(Clock), .Q(Q0), .reset(Clear_b));  // open: Qn, preset
  and and_1 (and_1_out, Enable, Q0);
  T_Flip_Flop t_ff_2 (.T(and_1_out), .clk(Clock), .Q(Q1), .reset(Clear_b));  // open: Qn, preset
  and and_2 (and_2_out, and_1_out, Q1);
  T_Flip_Flop t_ff_3 (.T(and_2_out), .clk(Clock), .Q(Q2), .reset(Clear_b));  // open: Qn, preset
  and and_3 (and_3_out, and_2_out, Q2);
  T_Flip_Flop t_ff_4 (.T(and_3_out), .clk(Clock), .Q(Q3), .reset(Clear_b));  // open: Qn, preset
  // AND_Gate and_4 has open pins: in0=and_3_out, in1=Q3, out=open
endmodule

module shifterBit (
  input  load_val,
  input  in1,
  input  shift,
  input  load_n,
  input  clk,
  input  reset,
  output Q
);

  wire mux2to1_1_m, mux2to1_2_m;

  mux2to1 mux2to1_1 (.x(Q), .y(in1), .s(shift), .m(mux2to1_1_m));
  mux2to1 mux2to1_2 (.x(load_val), .y(mux2to1_1_m), .s(load_n), .m(mux2to1_2_m));
  D_Flip_Flop d_ff_1 (.D(mux2to1_2_m), .clk(clk), .Q(Q), .reset(reset));  // open: Qn, preset
endmodule

module gated_D (
  input  D,
  input  Clk,
  output Qa,
  output Qb
);

  wire nand_1_out, nand_2_out, not_1_out;

  not not_1 (not_1_out, D);
  nand nand_1 (nand_1_out, D, Clk);
  nand nand_2 (nand_2_out, Clk, not_1_out);
  nand nand_3 (Qa, nand_1_out, Qb);
  nand nand_4 (Qb, Qa, nand_2_out);
endmodule

module flip_flop (
  input  D,
  input  Clk,
  output Q
);

  wire gated_d_1_qa, not_1_out;

  not not_1 (not_1_out, Clk);
  gated_D gated_d_1 (.D(D), .Clk(Clk), .Qa(gated_d_1_qa));  // open: Qb
  gated_D gated_d_2 (.D(gated_d_1_qa), .Clk(not_1_out), .Qa(Q));  // open: Qb
endmodule

module FourBit_Adder (
  input  cin,
  input  [3:0] A,
  input  [3:0] B,
  output S0,
  output S1,
  output S2,
  output S3,
  output cout
);

  wire full_adder_circut_1_c0, full_adder_circut_2_c0, full_adder_circut_3_c0;

  Full_Adder_Circut full_adder_circut_1 (.Ci(cin), .a(A[0]), .b(B[0]), .s(S0), .c0(full_adder_circut_1_c0));
  Full_Adder_Circut full_adder_circut_2 (
    .Ci(full_adder_circut_1_c0), .a(A[1]), .b(B[1]), .s(S1), .c0(full_adder_circut_2_c0));
  Full_Adder_Circut full_adder_circut_3 (
    .Ci(full_adder_circut_2_c0), .a(A[2]), .b(B[2]), .s(S2), .c0(full_adder_circut_3_c0));
  Full_Adder_Circut full_adder_circut_4 (.Ci(full_adder_circut_3_c0), .a(A[3]), .b(B[3]), .s(S3), .c0(cout));
endmodule

module multiplexor7 (
  input  [9:0] SW,
  output LEDR0
);

  Multiplexer #(.enable("false"), .select(3)) multiplexer_1 (
    .in0(SW[0]), .in1(SW[1]), .in2(SW[2]), .in3(SW[3]), .in4(SW[4]), .in5(SW[5]), .in6(SW[6]), .in7(1'b0),
    .out(LEDR0), .sel(SW[9:7]));
endmodule

module ALU_main_lab4 (
  input  WE,
  input  [3:0] A,
  input  [2:0] selector,
  input  C,
  input  R,
  output [7:0] out_6
);

  wire hex_decoder_submain_1_out_5, hex_decoder_submain_1_out_6, hex_decoder_submain_1_out_7,
       hex_decoder_submain_1_out_8, hex_decoder_submain_1_out_9, hex_decoder_submain_1_out_10,
       hex_decoder_submain_1_out_11, hex_decoder_submain_2_out_5, hex_decoder_submain_2_out_6,
       hex_decoder_submain_2_out_7, hex_decoder_submain_2_out_8, hex_decoder_submain_2_out_9,
       hex_decoder_submain_2_out_10, hex_decoder_submain_2_out_11, hex_decoder_submain_3_out_5,
       hex_decoder_submain_3_out_6, hex_decoder_submain_3_out_7, hex_decoder_submain_3_out_8,
       hex_decoder_submain_3_out_9, hex_decoder_submain_3_out_10, hex_decoder_submain_3_out_11;
  wire [7:0] alu_submain_1_output1;

  HEX_decoder_submain hex_decoder_submain_1 (
    .c3(A[3]), .c2(A[2]), .c1(A[1]), .c0(A[0]), .out_5(hex_decoder_submain_1_out_5),
    .out_6(hex_decoder_submain_1_out_6), .out_7(hex_decoder_submain_1_out_7),
    .out_8(hex_decoder_submain_1_out_8), .out_9(hex_decoder_submain_1_out_9),
    .out_10(hex_decoder_submain_1_out_10), .out_11(hex_decoder_submain_1_out_11));
  _7_Segment_Display #(.active("false")) u_7_segment_display_1 (
    .g(hex_decoder_submain_1_out_11), .f(hex_decoder_submain_1_out_10), .a(hex_decoder_submain_1_out_5),
    .b(hex_decoder_submain_1_out_6), .e(hex_decoder_submain_1_out_9), .d(hex_decoder_submain_1_out_8),
    .c(hex_decoder_submain_1_out_7));  // open: dp
  Register register_1 (.D(alu_submain_1_output1), .en(WE), .clk(C), .Q(out_6), .clr(R));
  ALU_submain alu_submain_1 (.A(A), .B(out_6[3:0]), .selector(selector), .output1(alu_submain_1_output1));
  HEX_decoder_submain hex_decoder_submain_2 (
    .c3(out_6[3]), .c2(out_6[2]), .c1(out_6[1]), .c0(out_6[0]), .out_5(hex_decoder_submain_2_out_5),
    .out_6(hex_decoder_submain_2_out_6), .out_7(hex_decoder_submain_2_out_7),
    .out_8(hex_decoder_submain_2_out_8), .out_9(hex_decoder_submain_2_out_9),
    .out_10(hex_decoder_submain_2_out_10), .out_11(hex_decoder_submain_2_out_11));
  HEX_decoder_submain hex_decoder_submain_3 (
    .c3(out_6[7]), .c2(out_6[6]), .c1(out_6[5]), .c0(out_6[4]), .out_5(hex_decoder_submain_3_out_5),
    .out_6(hex_decoder_submain_3_out_6), .out_7(hex_decoder_submain_3_out_7),
    .out_8(hex_decoder_submain_3_out_8), .out_9(hex_decoder_submain_3_out_9),
    .out_10(hex_decoder_submain_3_out_10), .out_11(hex_decoder_submain_3_out_11));
  _7_Segment_Display #(.active("false")) u_7_segment_display_2 (
    .g(hex_decoder_submain_3_out_11), .f(hex_decoder_submain_3_out_10), .a(hex_decoder_submain_3_out_5),
    .b(hex_decoder_submain_3_out_6), .e(hex_decoder_submain_3_out_9), .d(hex_decoder_submain_3_out_8),
    .c(hex_decoder_submain_3_out_7));  // open: dp
  _7_Segment_Display #(.active("false")) u_7_segment_display_3 (
    .g(hex_decoder_submain_2_out_11), .f(hex_decoder_submain_2_out_10), .a(hex_decoder_submain_2_out_5),
    .b(hex_decoder_submain_2_out_6), .e(hex_decoder_submain_2_out_9), .d(hex_decoder_submain_2_out_8),
    .c(hex_decoder_submain_2_out_7));  // open: dp
endmodule

module value0 (
  input  [3:0] A,
  input  [3:0] B,
  output [7:0] out_3
);

  wire [4:0] fourbit_adder_1_s0;

  FourBit_Adder fourbit_adder_1 (
    .cin(1'b0), .A(A), .B(4'b0001), .S0(fourbit_adder_1_s0[0]), .S1(fourbit_adder_1_s0[1]),
    .S2(fourbit_adder_1_s0[2]), .S3(fourbit_adder_1_s0[3]), .cout(fourbit_adder_1_s0[4]));
  assign out_3 = {{3{1'b0}}, fourbit_adder_1_s0};  // Bit_Extender bit_extender_1
endmodule

module value1 (
  input  [3:0] A,
  input  [3:0] B,
  output [7:0] out_3
);

  wire [4:0] fourbit_adder_1_s0;

  FourBit_Adder fourbit_adder_1 (
    .cin(1'b0), .A(A), .B(B), .S0(fourbit_adder_1_s0[0]), .S1(fourbit_adder_1_s0[1]),
    .S2(fourbit_adder_1_s0[2]), .S3(fourbit_adder_1_s0[3]), .cout(fourbit_adder_1_s0[4]));
  assign out_3 = {{3{1'b0}}, fourbit_adder_1_s0};  // Bit_Extender bit_extender_1
endmodule

module value2 (
  input  [3:0] A,
  input  [3:0] B,
  output [7:0] out_3
);

  wire [3:0] adder_1_out;
  wire [4:4] adder_1_cout;

  Adder #(.width(4)) adder_1 (.a(A), .b(B), .out(adder_1_out), .cin(1'b0), .cout(adder_1_cout[4]));
  assign out_3 = {{3{1'b0}}, {adder_1_cout[4], adder_1_out}};  // Bit_Extender bit_extender_1
endmodule

module value3 (
  input  [3:0] A,
  input  [3:0] B,
  output [7:0] out_3
);

  assign out_3[3:0] = A ^ B;  // XOR_Gate xor_1, 4 bits wide
  assign out_3[7:4] = A | B;  // OR_Gate or_1, 4 bits wide
endmodule

module value4 (
  input  [3:0] A,
  input  [3:0] B,
  output [7:0] out_3
);

  wire or_2_out;
  wire [3:0] or_1_out;

  assign or_1_out = A | B;  // OR_Gate or_1, 4 bits wide
  or or_2 (or_2_out, or_1_out[0], or_1_out[1], or_1_out[2], or_1_out[3]);
  assign out_3 = {{7{1'b0}}, or_2_out};  // Bit_Extender bit_extender_1
endmodule

module value5 (
  input  [3:0] B,
  input  [3:0] A,
  output [7:0] output1
);

  wire [8:0] bit_extender_1_out;
  wire [8:8] shifter_1_out;

  assign bit_extender_1_out = {{5{1'b0}}, B};  // Bit_Extender bit_extender_1
  Shifter #(.width(9)) shifter_1 (.in(bit_extender_1_out), .\dist (A), .out({shifter_1_out[8], output1}));
endmodule

module value6 (
  input  [3:0] B,
  input  [3:0] A,
  output [7:0] output1
);

  wire [15:0] bit_extender_1_out, shifter_1_out;
  wire [15:8] shifter_2_out;

  assign bit_extender_1_out = {{12{1'b0}}, B};  // Bit_Extender bit_extender_1
  Shifter #(.width(16)) shifter_1 (.in(bit_extender_1_out), .\dist (4'b0101), .out(shifter_1_out));
  Shifter #(.shift("lr"), .width(16)) shifter_2 (.in(shifter_1_out), .\dist (A), .out({shifter_2_out, output1}));
endmodule

module value7 (
  input  [3:0] A,
  input  [3:0] B,
  output [7:0] output1
);

  Multiplier #(.width(4)) multiplier_1 (.a(A), .b(B), .out(output1[3:0]), .cin(4'b0000), .cout(output1[7:4]));
endmodule

module Full_Adder_Circut (
  input  Ci,
  input  a,
  input  b,
  output s,
  output c0
);

  wire xor_1_out;

  xor xor_1 (xor_1_out, a, b);
  Multiplexer #(.enable("false")) multiplexer_1 (.in0(b), .in1(Ci), .out(c0), .sel(xor_1_out));
  xor xor_2 (s, Ci, xor_1_out);
endmodule

module ALU_submain (
  input  [3:0] A,
  input  [3:0] B,
  input  [2:0] selector,
  output [7:0] output1
);

  wire [7:0] value0_1_out_3, value1_1_out_3, value2_1_out_3, value3_1_out_3, value4_1_out_3,
       value5_1_output1, value6_1_output1, value7_1_output1;

  value0 value0_1 (.A(A), .B(B), .out_3(value0_1_out_3));
  value1 value1_1 (.A(A), .B(B), .out_3(value1_1_out_3));
  value2 value2_1 (.A(A), .B(B), .out_3(value2_1_out_3));
  value3 value3_1 (.A(A), .B(B), .out_3(value3_1_out_3));
  value4 value4_1 (.A(A), .B(B), .out_3(value4_1_out_3));
  value5 value5_1 (.B(B), .A(A), .output1(value5_1_output1));
  value6 value6_1 (.B(B), .A(A), .output1(value6_1_output1));
  value7 value7_1 (.A(A), .B(B), .output1(value7_1_output1));
  Multiplexer #(.enable("false"), .select(3), .width(8)) multiplexer_1 (
    .in0(value0_1_out_3), .in1(value1_1_out_3), .in2(value2_1_out_3), .in3(value3_1_out_3),
    .in4(value4_1_out_3), .in5(value5_1_output1), .in6(value6_1_output1), .in7(value7_1_output1),
    .out(output1), .sel(selector));
endmodule

module ALU_main (
  input  [3:0] A,
  input  [3:0] B,
  input  [2:0] selector,
  output [7:0] output1
);

  wire hex_decoder_submain_1_out_5, hex_decoder_submain_1_out_6, hex_decoder_submain_1_out_7,
       hex_decoder_submain_1_out_8, hex_decoder_submain_1_out_9, hex_decoder_submain_1_out_10,
       hex_decoder_submain_1_out_11, hex_decoder_submain_2_out_5, hex_decoder_submain_2_out_6,
       hex_decoder_submain_2_out_7, hex_decoder_submain_2_out_8, hex_decoder_submain_2_out_9,
       hex_decoder_submain_2_out_10, hex_decoder_submain_2_out_11, hex_decoder_submain_3_out_5,
       hex_decoder_submain_3_out_6, hex_decoder_submain_3_out_7, hex_decoder_submain_3_out_8,
       hex_decoder_submain_3_out_9, hex_decoder_submain_3_out_10, hex_decoder_submain_3_out_11,
       hex_decoder_submain_4_out_5, hex_decoder_submain_4_out_6, hex_decoder_submain_4_out_7,
       hex_decoder_submain_4_out_8, hex_decoder_submain_4_out_9, hex_decoder_submain_4_out_10,
       hex_decoder_submain_4_out_11;

  HEX_decoder_submain hex_decoder_submain_1 (
    .c3(A[3]), .c2(A[2]), .c1(A[1]), .c0(A[0]), .out_5(hex_decoder_submain_1_out_5),
    .out_6(hex_decoder_submain_1_out_6), .out_7(hex_decoder_submain_1_out_7),
    .out_8(hex_decoder_submain_1_out_8), .out_9(hex_decoder_submain_1_out_9),
    .out_10(hex_decoder_submain_1_out_10), .out_11(hex_decoder_submain_1_out_11));
  HEX_decoder_submain hex_decoder_submain_2 (
    .c3(B[3]), .c2(B[2]), .c1(B[1]), .c0(B[0]), .out_5(hex_decoder_submain_2_out_5),
    .out_6(hex_decoder_submain_2_out_6), .out_7(hex_decoder_submain_2_out_7),
    .out_8(hex_decoder_submain_2_out_8), .out_9(hex_decoder_submain_2_out_9),
    .out_10(hex_decoder_submain_2_out_10), .out_11(hex_decoder_submain_2_out_11));
  _7_Segment_Display #(.active("false")) u_7_segment_display_1 (
    .g(hex_decoder_submain_1_out_11), .f(hex_decoder_submain_1_out_10), .a(hex_decoder_submain_1_out_5),
    .b(hex_decoder_submain_1_out_6), .e(hex_decoder_submain_1_out_9), .d(hex_decoder_submain_1_out_8),
    .c(hex_decoder_submain_1_out_7));  // open: dp
  _7_Segment_Display #(.active("false")) u_7_segment_display_2 (
    .g(hex_decoder_submain_2_out_11), .f(hex_decoder_submain_2_out_10), .a(hex_decoder_submain_2_out_5),
    .b(hex_decoder_submain_2_out_6), .e(hex_decoder_submain_2_out_9), .d(hex_decoder_submain_2_out_8),
    .c(hex_decoder_submain_2_out_7));  // open: dp
  ALU_submain alu_submain_1 (.A(A), .B(B), .selector(selector), .output1(output1));
  LED led_1 (.in(output1[0]));
  LED led_2 (.in(output1[1]));
  LED led_3 (.in(output1[2]));
  LED led_4 (.in(output1[3]));
  LED led_5 (.in(output1[4]));
  LED led_6 (.in(output1[5]));
  LED led_7 (.in(output1[6]));
  LED led_8 (.in(output1[7]));
  HEX_decoder_submain hex_decoder_submain_3 (
    .c3(output1[3]), .c2(output1[2]), .c1(output1[1]), .c0(output1[0]), .out_5(hex_decoder_submain_3_out_5),
    .out_6(hex_decoder_submain_3_out_6), .out_7(hex_decoder_submain_3_out_7),
    .out_8(hex_decoder_submain_3_out_8), .out_9(hex_decoder_submain_3_out_9),
    .out_10(hex_decoder_submain_3_out_10), .out_11(hex_decoder_submain_3_out_11));
  HEX_decoder_submain hex_decoder_submain_4 (
    .c3(output1[7]), .c2(output1[6]), .c1(output1[5]), .c0(output1[4]), .out_5(hex_decoder_submain_4_out_5),
    .out_6(hex_decoder_submain_4_out_6), .out_7(hex_decoder_submain_4_out_7),
    .out_8(hex_decoder_submain_4_out_8), .out_9(hex_decoder_submain_4_out_9),
    .out_10(hex_decoder_submain_4_out_10), .out_11(hex_decoder_submain_4_out_11));
  _7_Segment_Display #(.active("false")) u_7_segment_display_3 (
    .g(hex_decoder_submain_4_out_11), .f(hex_decoder_submain_4_out_10), .a(hex_decoder_submain_4_out_5),
    .b(hex_decoder_submain_4_out_6), .e(hex_decoder_submain_4_out_9), .d(hex_decoder_submain_4_out_8),
    .c(hex_decoder_submain_4_out_7));  // open: dp
  _7_Segment_Display #(.active("false")) u_7_segment_display_4 (
    .g(hex_decoder_submain_3_out_11), .f(hex_decoder_submain_3_out_10), .a(hex_decoder_submain_3_out_5),
    .b(hex_decoder_submain_3_out_6), .e(hex_decoder_submain_3_out_9), .d(hex_decoder_submain_3_out_8),
    .c(hex_decoder_submain_3_out_7));  // open: dp
endmodule

module mux2to1 (
  input  x,
  input  y,
  input  s,
  output m
);

  Multiplexer #(.enable("false")) multiplexer_1 (.in0(x), .in1(y), .out(m), .sel(s));
endmodule
