// Logisim project lab6.circ as structural Verilog: 26 circuits, main circuit part_1_state_table
module part_1_state_table (
  input  [2:0] curr_state,
  input  w,
  output [2:0] next_state
);

  wire and_1_out, and_2_out, and_3_out, and_4_out, and_5_out, and_6_out, and_7_out, and_8_out, and_9_out,
       and_10_out, not_1_out, not_2_out, not_3_out, not_4_out;

  not not_1 (not_1_out, w);
  not not_2 (not_2_out, curr_state[0]);
  not not_3 (not_3_out, curr_state[1]);
  not not_4 (not_4_out, curr_state[2]);
  and and_1 (and_1_out, w, not_2_out, not_4_out);
  and and_2 (and_2_out, w, curr_state[1], not_4_out);
  and and_3 (and_3_out, curr_state[2], curr_state[0], w);
  and and_4 (and_4_out, curr_state[1], not_2_out, w);
  and and_5 (and_5_out, curr_state[2], not_2_out, w);
  and and_6 (and_6_out, not_3_out, not_4_out, curr_state[0], w);
  and and_7 (and_7_out, curr_state[0], curr_state[1]);
  and and_8 (and_8_out, curr_state[2], curr_state[0]);
  and and_9 (and_9_out, not_4_out, curr_state[1], not_1_out);
  and and_10 (and_10_out, curr_state[2], not_3_out, w);
  or or_1 (next_state[0], and_1_out, and_2_out, and_3_out);
  or or_2 (next_state[1], and_4_out, and_5_out, and_6_out);
  or or_3 (next_state[2], and_7_out, and_8_out, and_9_out, and_10_out);

  // Notes on the sheet:
  //   This is the state table, refer to the state diagram. To be completed by you. 
endmodule

module part_1_FSM (
  input  W,
  input  Enable,
  input  Reset,
  output z
);

  wire and_1_out, and_2_out, Clk_out, not_1_out, not_2_out;
  wire [2:0] state_q, state_table_next_state;

  part_1_state_table state_table (.curr_state(state_q), .w(W), .next_state(state_table_next_state));
  Register #(.width(3)) state (.D(state_table_next_state), .en(Enable), .clk(Clk_out), .Q(state_q), .clr(Reset));
  Clock Clk (.out(Clk_out));
  not not_1 (not_1_out, state_q[1]);
  not not_2 (not_2_out, state_q[0]);
  and and_1 (and_1_out, state_q[0], not_1_out, state_q[2]);
  and and_2 (and_2_out, not_2_out, state_q[1], state_q[2]);
  or or_1 (z, and_1_out, and_2_out);

  // Notes on the sheet:
  //   your state table
  //   state register
  //   output logic (to be completed by you)
endmodule

module part_2_datapath (
  input  ld_alu_out,
  input  [7:0] data_in,
  input  clk,
  input  ld_c,
  input  ld_x,
  input  ld_a,
  input  ld_b,
  input  Reset,
  input  [1:0] alu_select_a,
  input  [1:0] alu_select_b,
  input  alu_op,
  input  ld_r,
  output [7:0] R_B_val,
  output [7:0] R_A_val,
  output [7:0] R_X_val,
  output [7:0] R_C_val,
  output [7:0] data_result
);

  wire [7:0] multiplexer_1_out, multiplexer_2_out, multiplexer_3_out, multiplexer_4_out, part_2_alu_1_alu_out;

  Register R_C (.D(data_in), .en(ld_c), .clk(clk), .Q(R_C_val), .clr(Reset));
  Register R_X (.D(data_in), .en(ld_x), .clk(clk), .Q(R_X_val), .clr(Reset));
  Multiplexer #(.enable("false"), .select(2), .width(8)) multiplexer_1 (
    .in0(R_A_val), .in1(R_B_val), .in2(R_C_val), .in3(R_X_val), .out(multiplexer_1_out), .sel(alu_select_a));
  Multiplexer #(.enable("false"), .width(8)) multiplexer_2 (
    .in0(data_in), .in1(part_2_alu_1_alu_out), .out(multiplexer_2_out), .sel(ld_alu_out));
  Register R_A (.D(multiplexer_2_out), .en(ld_a), .clk(clk), .Q(R_A_val), .clr(Reset));
  Multiplexer #(.enable("false"), .select(2), .width(8)) multiplexer_3 (
    .in0(R_A_val), .in1(R_B_val), .in2(R_C_val), .in3(R_X_val), .out(multiplexer_3_out), .sel(alu_select_b));
  part_2_ALU part_2_alu_1 (
    .input_1(multiplexer_1_out), .input_2(multiplexer_3_out), .ALU_op(alu_op), .ALU_out(part_2_alu_1_alu_out));
  Multiplexer #(.enable("false"), .width(8)) multiplexer_4 (
    .in0(data_in), .in1(part_2_alu_1_alu_out), .out(multiplexer_4_out), .sel(ld_alu_out));
  Register R_B (.D(multiplexer_4_out), .en(ld_b), .clk(clk), .Q(R_B_val), .clr(Reset));
  Register R_R (.D(part_2_alu_1_alu_out), .en(ld_r), .clk(clk), .Q(data_result), .clr(Reset));
endmodule

module part_2_ALU (
  input  [7:0] input_1,
  input  [7:0] input_2,
  input  ALU_op,
  output [7:0] ALU_out
);

  wire [7:0] adder_1_out, multiplier_1_out;

  Adder adder_1 (.a(input_1), .b(input_2), .out(adder_1_out));  // open: cin, cout
  Multiplier multiplier_1 (.a(input_1), .b(input_2), .out(multiplier_1_out));  // open: cin, cout
  Multiplexer #(.enable("false"), .width(8)) multiplexer_1 (
    .in0(adder_1_out), .in1(multiplier_1_out), .out(ALU_out), .sel(ALU_op));
endmodule

module part_2_state_table (
  input  [3:0] state,
  output ld_a,
  output ld_b,
  output ld_c,
  output ld_x,
  output [1:0] alu_select_a,
  output [1:0] alu_select_b,
  output ld_alu_out,
  output alu_op,
  output ld_r,
  output [3:0] next_state
);

  part_2_ld_a_state_table part_2_ld_a_state_table_1 (.state(state), .ld_a(ld_a));
  part_2_ld_b_state_table part_2_ld_b_state_table_1 (.state(state), .ld_b(ld_b));
  part_2_ld_c_state_table part_2_ld_c_state_table_1 (.state(state), .ld_c(ld_c));
  part_2_ld_x_state_table part_2_ld_x_state_table_1 (.state(state), .ld_x(ld_x));
  part_2_alu_select_a_state_table part_2_alu_select_a_state_table_1 (.state(state), .alu_select_a(alu_select_a));
  part_2_alu_select_b_state_table part_2_alu_select_b_state_table_1 (.state(state), .alu_select_b(alu_select_b));
  part_2_ld_alu_out_state_table part_2_ld_alu_out_state_table_1 (.state(state), .ld_alu_out(ld_alu_out));
  part_2_alu_op_state_table part_2_alu_op_state_table_1 (.state(state), .alu_op(alu_op));
  part_2_ld_r_state_table part_2_ld_r_state_table_1 (.state(state), .ld_r(ld_r));
  part_2_next_state part_2_next_state_1 (.state(state), .next_state(next_state));
endmodule

module part_2_ld_a_state_table (
  input  [3:0] state,
  output ld_a
);

  wire and_1_out, and_2_out, not_1_out, not_2_out, not_3_out, not_4_out, not_5_out;

  not not_1 (not_1_out, state[3]);
  not not_2 (not_2_out, state[2]);
  not not_3 (not_3_out, state[1]);
  not not_4 (not_4_out, state[0]);
  not not_5 (not_5_out, state[3]);
  and and_1 (and_1_out, not_1_out, not_2_out, not_3_out, not_4_out);
  and and_2 (and_2_out, not_5_out, state[2], state[1]);
  or or_1 (ld_a, and_1_out, and_2_out);
endmodule

module part_2_ld_b_state_table (
  input  [3:0] state,
  output ld_b
);

  wire and_1_out, and_2_out, not_1_out, not_2_out;

  not not_1 (not_1_out, state[1]);
  not not_2 (not_2_out, state[3]);
  and and_1 (and_1_out, state[0], not_1_out, not_2_out);
  and and_2 (and_2_out, not_1_out, state[2], not_2_out);
  or or_1 (ld_b, and_1_out, and_2_out);
endmodule

module part_2_ld_c_state_table (
  input  [3:0] state,
  output ld_c
);

  wire not_1_out, not_2_out, not_3_out;

  not not_1 (not_1_out, state[0]);
  not not_2 (not_2_out, state[2]);
  not not_3 (not_3_out, state[3]);
  and and_1 (ld_c, not_1_out, state[1], not_2_out, not_3_out);
endmodule

module part_2_ld_x_state_table (
  input  [3:0] state,
  output ld_x
);

  wire not_1_out, not_2_out;

  not not_1 (not_1_out, state[2]);
  not not_2 (not_2_out, state[3]);
  and and_1 (ld_x, state[0], state[1], not_1_out, not_2_out);
endmodule

module part_2_alu_select_a_state_table (
  input  [3:0] state,
  output [1:0] alu_select_a
);

  wire not_1_out, not_2_out;

  not not_1 (not_1_out, state[0]);
  not not_2 (not_2_out, state[3]);
  and and_1 (alu_select_a[1], not_1_out, state[2], not_2_out);

  assign alu_select_a[0] = alu_select_a[1];
endmodule

module part_2_alu_select_b_state_table (
  input  [3:0] state,
  output [1:0] alu_select_b
);

  wire and_1_out, and_2_out, and_3_out, not_1_out, not_2_out, not_3_out, not_4_out, not_5_out;

  not not_1 (not_1_out, state[2]);
  not not_2 (not_2_out, state[0]);
  not not_3 (not_3_out, state[1]);
  not not_4 (not_4_out, state[3]);
  not not_5 (not_5_out, state[3]);
  and and_1 (and_1_out, not_2_out, not_3_out, not_1_out, state[3]);
  and and_2 (and_2_out, not_2_out, state[2], not_4_out);
  and and_3 (and_3_out, not_3_out, state[2], not_4_out);
  and and_4 (alu_select_b[1], state[1], state[2], not_5_out);
  or or_1 (alu_select_b[0], and_1_out, and_2_out, and_3_out);
endmodule

module part_2_ld_alu_out_state_table (
  input  [3:0] state,
  output ld_alu_out
);

  wire not_1_out;

  not not_1 (not_1_out, state[3]);
  and and_1 (ld_alu_out, state[2], not_1_out);
endmodule

module part_2_alu_op_state_table (
  input  [3:0] state,
  output alu_op
);

  wire and_1_out, and_2_out, not_1_out, not_2_out, not_3_out;

  not not_1 (not_1_out, state[1]);
  not not_2 (not_2_out, state[0]);
  not not_3 (not_3_out, state[3]);
  and and_1 (and_1_out, not_2_out, not_1_out, state[2], not_3_out);
  and and_2 (and_2_out, state[1], state[2], not_3_out);
  or or_1 (alu_op, and_1_out, and_2_out);
endmodule

module part_2_ld_r_state_table (
  input  [3:0] state,
  output ld_r
);

  wire not_1_out, not_2_out, not_3_out;

  not not_1 (not_1_out, state[2]);
  not not_2 (not_2_out, state[0]);
  not not_3 (not_3_out, state[1]);
  and and_1 (ld_r, not_2_out, not_3_out, not_1_out, state[3]);
endmodule

module part_2_next_state (
  input  [3:0] state,
  output [3:0] next_state
);

  wire and_2_out, and_3_out, and_4_out, and_5_out, and_6_out, not_1_out, not_2_out, not_3_out, not_4_out,
       not_5_out, not_6_out, not_7_out, not_8_out, not_9_out, not_10_out, not_11_out, not_12_out, not_13_out;

  not not_1 (not_1_out, state[0]);
  not not_2 (not_2_out, state[3]);
  not not_3 (not_3_out, state[1]);
  not not_4 (not_4_out, state[3]);
  not not_5 (not_5_out, state[0]);
  not not_6 (not_6_out, state[3]);
  not not_7 (not_7_out, state[0]);
  not not_8 (not_8_out, state[3]);
  not not_9 (not_9_out, state[1]);
  not not_10 (not_10_out, state[3]);
  not not_11 (not_11_out, state[2]);
  not not_12 (not_12_out, state[3]);
  not not_13 (not_13_out, state[3]);
  and and_1 (next_state[0], not_1_out, not_2_out);
  and and_2 (and_2_out, state[0], not_3_out, not_4_out);
  and and_3 (and_3_out, not_5_out, state[1], not_6_out);
  and and_4 (and_4_out, not_7_out, state[2], not_8_out);
  and and_5 (and_5_out, not_9_out, state[2], not_10_out);
  and and_6 (and_6_out, state[0], state[1], not_11_out, not_12_out);
  and and_7 (next_state[3], state[0], state[1], state[2], not_13_out);
  or or_1 (next_state[1], and_2_out, and_3_out);
  or or_2 (next_state[2], and_4_out, and_5_out, and_6_out);
endmodule

module part_2_FSM (
  input  [7:0] data_in,
  input  Enable,
  input  Reset
);

  wire Clk_out, not_1_out, part_2_state_table_1_alu_op, part_2_state_table_1_ld_a,
       part_2_state_table_1_ld_alu_out, part_2_state_table_1_ld_b, part_2_state_table_1_ld_c,
       part_2_state_table_1_ld_r, part_2_state_table_1_ld_x;
  wire [1:0] part_2_state_table_1_alu_select_a, part_2_state_table_1_alu_select_b;
  wire [3:0] part_2_state_table_1_next_state, register_1_q;
  wire [7:0] part_2_datapath_1_data_result, part_2_datapath_1_r_a_val, part_2_datapath_1_r_b_val,
       part_2_datapath_1_r_c_val, part_2_datapath_1_r_x_val;

  part_2_state_table part_2_state_table_1 (
    .state(register_1_q), .ld_a(part_2_state_table_1_ld_a), .ld_b(part_2_state_table_1_ld_b),
    .ld_c(part_2_state_table_1_ld_c), .ld_x(part_2_state_table_1_ld_x),
    .alu_select_a(part_2_state_table_1_alu_select_a), .alu_select_b(part_2_state_table_1_alu_select_b),
    .ld_alu_out(part_2_state_table_1_ld_alu_out), .alu_op(part_2_state_table_1_alu_op),
    .ld_r(part_2_state_table_1_ld_r), .next_state(part_2_state_table_1_next_state));
  Register #(.width(4)) register_1 (
    .D(part_2_state_table_1_next_state), .en(Enable), .clk(Clk_out), .Q(register_1_q), .clr(not_1_out));
  not not_1 (not_1_out, Reset);
  Clock Clk (.out(Clk_out));
  Hex_Digit_Display hex_digit_display_1 (.value(data_in[7:4]));  // open: dp
  Hex_Digit_Display hex_digit_display_2 (.value(data_in[3:0]));  // open: dp
  part_2_datapath part_2_datapath_1 (
    .ld_alu_out(part_2_state_table_1_ld_alu_out), .data_in(data_in), .clk(Clk_out),
    .ld_c(part_2_state_table_1_ld_c), .ld_x(part_2_state_table_1_ld_x), .ld_a(part_2_state_table_1_ld_a),
    .ld_b(part_2_state_table_1_ld_b), .Reset(not_1_out), .alu_select_a(part_2_state_table_1_alu_select_a),
    .alu_select_b(part_2_state_table_1_alu_select_b), .alu_op(part_2_state_table_1_alu_op),
    .ld_r(part_2_state_table_1_ld_r), .R_B_val(part_2_datapath_1_r_b_val),
    .R_A_val(part_2_datapath_1_r_a_val), .R_X_val(part_2_datapath_1_r_x_val),
    .R_C_val(part_2_datapath_1_r_c_val), .data_result(part_2_datapath_1_data_result));
  Hex_Digit_Display hex_digit_display_3 (.value(part_2_datapath_1_r_b_val[7:4]));  // open: dp
  Hex_Digit_Display hex_digit_display_4 (.value(part_2_datapath_1_r_b_val[3:0]));  // open: dp
  Hex_Digit_Display hex_digit_display_5 (.value(part_2_datapath_1_r_c_val[7:4]));  // open: dp
  Hex_Digit_Display hex_digit_display_6 (.value(part_2_datapath_1_data_result[7:4]));  // open: dp
  Hex_Digit_Display hex_digit_display_7 (.value(part_2_datapath_1_r_a_val[7:4]));  // open: dp
  Hex_Digit_Display hex_digit_display_8 (.value(part_2_datapath_1_r_x_val[7:4]));  // open: dp
  Hex_Digit_Display hex_digit_display_9 (.value(part_2_datapath_1_r_x_val[3:0]));  // open: dp
  Hex_Digit_Display hex_digit_display_10 (.value(part_2_datapath_1_r_c_val[3:0]));  // open: dp
  Hex_Digit_Display hex_digit_display_11 (.value(part_2_datapath_1_data_result[3:0]));  // open: dp
  LED led_1 (.in(part_2_datapath_1_data_result[0]));
  LED led_2 (.in(part_2_datapath_1_data_result[1]));
  LED led_3 (.in(part_2_datapath_1_data_result[2]));
  LED led_4 (.in(part_2_datapath_1_data_result[3]));
  LED led_5 (.in(part_2_datapath_1_data_result[4]));
  LED led_6 (.in(part_2_datapath_1_data_result[5]));
  LED led_7 (.in(part_2_datapath_1_data_result[6]));
  LED led_8 (.in(part_2_datapath_1_data_result[7]));
  Hex_Digit_Display hex_digit_display_12 (.value(part_2_datapath_1_r_a_val[3:0]));  // open: dp
endmodule

module part3_datapath (
  input  ld_alu_out,
  input  [7:0] data_in,
  input  clk,
  input  ld_sor,
  input  ld_end,
  input  ld_reg,
  input  Reset,
  input  ld_r,
  output [7:0] R_dend_val,
  output [7:0] R_Reg_val,
  output [7:0] R_sor_val,
  output [7:0] remainder,
  output [7:0] quotient
);

  wire [3:0] multiplexer_1_out, one_operation_1_output_div, R_dividend_q, R_quotient_q;
  wire [4:0] multiplexer_2_out, one_operation_1_output_reg, R_divisor_q, R_reg_q, R_Remainder_q;

  Register #(.width(5)) R_divisor (.D(data_in[4:0]), .en(ld_sor), .clk(clk), .Q(R_divisor_q), .clr(Reset));
  Multiplexer #(.enable("false"), .width(4)) multiplexer_1 (
    .in0(data_in[3:0]), .in1(one_operation_1_output_div), .out(multiplexer_1_out), .sel(ld_alu_out));
  Register #(.width(4)) R_dividend (.D(multiplexer_1_out), .en(ld_end), .clk(clk), .Q(R_dividend_q), .clr(Reset));
  Multiplexer #(.enable("false"), .width(5)) multiplexer_2 (
    .in0({5{1'b0}}), .in1(one_operation_1_output_reg), .out(multiplexer_2_out), .sel(ld_alu_out));
  Register #(.width(5)) R_reg (.D(multiplexer_2_out), .en(ld_reg), .clk(clk), .Q(R_reg_q), .clr(Reset));
  one_operation one_operation_1 (
    .dividend(R_dividend_q), .regi(R_reg_q), .divisor(R_divisor_q), .output_div(one_operation_1_output_div),
    .output_reg(one_operation_1_output_reg));
  Register #(.width(4)) R_quotient (
    .D(one_operation_1_output_div), .en(ld_r), .clk(clk), .Q(R_quotient_q), .clr(Reset));
  assign R_Reg_val = {{3{1'b0}}, R_reg_q};  // Bit_Extender bit_extender_1
  assign R_sor_val = {{3{1'b0}}, R_divisor_q};  // Bit_Extender bit_extender_2
  Register #(.width(5)) R_Remainder (
    .D(one_operation_1_output_reg), .en(ld_r), .clk(clk), .Q(R_Remainder_q), .clr(Reset));
  assign R_dend_val = {{4{1'b0}}, R_dividend_q};  // Bit_Extender bit_extender_3
  assign remainder = {{3{1'b0}}, R_Remainder_q};  // Bit_Extender bit_extender_4
  assign quotient = {{4{1'b0}}, R_quotient_q};  // Bit_Extender bit_extender_5
endmodule

module one_operation (
  input  [3:0] dividend,
  input  [4:0] regi,
  input  [4:0] divisor,
  output [3:0] output_div,
  output [4:0] output_reg
);

  wire [4:0] adder_1_out, subtractor_1_out;
  wire [8:0] shifter_1_out;

  Shifter #(.width(9)) shifter_1 (
    .in({regi, dividend}), .\dist (4'b0001), .out({shifter_1_out[8:4], output_div[3:1], shifter_1_out[0]}));
  Subtractor #(.width(5)) subtractor_1 (
    .a(shifter_1_out[8:4]), .b(divisor), .out(subtractor_1_out));  // open: bin, bout
  Adder #(.width(5)) adder_1 (.a(subtractor_1_out), .b(divisor), .out(adder_1_out));  // open: cin, cout
  not not_1 (output_div[0], subtractor_1_out[4]);
  Multiplexer #(.enable("false"), .width(5)) multiplexer_1 (
    .in0(adder_1_out), .in1(subtractor_1_out), .out(output_reg), .sel(output_div[0]));
endmodule

module part_3_Id_sor_state_table (
  input  [2:0] state,
  output id_sor
);

  wire or_1_out;

  or or_1 (or_1_out, state[0], state[1], state[2]);
  not not_1 (id_sor, or_1_out);
endmodule

module part_3_Id_end_table (
  input  [2:0] state,
  output id_end
);

  or or_1 (id_end, state[0], state[1], state[2]);
endmodule

module part3_id_reg (
  input  [2:0] state,
  output id_reg
);

  wire and_1_out, not_1_out, not_2_out, not_3_out, or_1_out;

  or or_1 (or_1_out, state[0], state[1], state[2]);
  not not_1 (not_1_out, state[1]);
  and and_1 (and_1_out, state[0], not_1_out, not_2_out);
  not not_2 (not_2_out, state[2]);
  and and_2 (id_reg, or_1_out, not_3_out);
  not not_3 (not_3_out, and_1_out);
endmodule

module part3_id_out (
  input  [2:0] state,
  output id_out
);

  wire and_1_out, and_2_out, and_3_out, not_1_out, not_2_out, not_3_out;

  not not_1 (not_1_out, state[0]);
  not not_2 (not_2_out, state[2]);
  not not_3 (not_3_out, state[1]);
  and and_1 (and_1_out, not_1_out, state[1], not_2_out);
  and and_2 (and_2_out, state[0], state[1], not_2_out);
  and and_3 (and_3_out, not_1_out, not_3_out, state[2]);
  or or_1 (id_out, and_1_out, and_2_out, and_3_out);
endmodule

module part3_idr (
  input  [2:0] state,
  output id_end
);

  wire not_1_out;

  not not_1 (not_1_out, state[1]);
  and and_1 (id_end, state[0], not_1_out, state[2]);
endmodule

module part3_state_table (
  input  [2:0] state,
  output ld_sor,
  output ld_end,
  output ld_reg,
  output id_out,
  output id_r,
  output [2:0] next_state
);

  part_3_Id_sor_state_table part_3_id_sor_state_table_1 (.state(state), .id_sor(ld_sor));
  part_3_Id_end_table part_3_id_end_table_1 (.state(state), .id_end(ld_end));
  part3_id_reg part3_id_reg_1 (.state(state), .id_reg(ld_reg));
  part3_id_out part3_id_out_1 (.state(state), .id_out(id_out));
  part3_idr part3_idr_1 (.state(state), .id_end(id_r));
  part3_next_state part3_next_state_1 (.state(state), .id_end(next_state));
endmodule

module part3_next_state (
  input  [2:0] state,
  output [2:0] id_end
);

  wire and_1_out, and_2_out, and_3_out, and_4_out, not_1_out, not_2_out;

  not not_1 (not_1_out, state[1]);
  not not_2 (not_2_out, state[2]);
  not not_3 (id_end[0], state[0]);
  and and_1 (and_1_out, state[0], not_1_out, not_2_out);
  and and_2 (and_2_out, id_end[0], state[1], not_2_out);
  and and_3 (and_3_out, state[0], state[1], not_2_out);
  and and_4 (and_4_out, id_end[0], not_1_out, state[2]);
  or or_1 (id_end[1], and_1_out, and_2_out);
  or or_2 (id_end[2], and_3_out, and_4_out);
endmodule

module part3_fsm (
  input  [7:0] data_in,
  input  Enable,
  input  Reset
);

  wire Clk_out, not_1_out, part3_state_table_1_id_out, part3_state_table_1_id_r, part3_state_table_1_ld_end,
       part3_state_table_1_ld_reg, part3_state_table_1_ld_sor;
  wire [2:0] part3_state_table_1_next_state, register_1_q;
  wire [7:0] part3_datapath_1_quotient, part3_datapath_1_r_dend_val, part3_datapath_1_r_reg_val,
       part3_datapath_1_r_sor_val, part3_datapath_1_remainder;

  part3_state_table part3_state_table_1 (
    .state(register_1_q), .ld_sor(part3_state_table_1_ld_sor), .ld_end(part3_state_table_1_ld_end),
    .ld_reg(part3_state_table_1_ld_reg), .id_out(part3_state_table_1_id_out),
    .id_r(part3_state_table_1_id_r), .next_state(part3_state_table_1_next_state));
  Register #(.width(3)) register_1 (
    .D(part3_state_table_1_next_state), .en(Enable), .clk(Clk_out), .Q(register_1_q), .clr(not_1_out));
  not not_1 (not_1_out, Reset);
  Clock Clk (.out(Clk_out));
  Hex_Digit_Display hex_digit_display_1 (.value(data_in[7:4]));  // open: dp
  Hex_Digit_Display hex_digit_display_2 (.value(data_in[3:0]));  // open: dp
  part3_datapath part3_datapath_1 (
    .ld_alu_out(part3_state_table_1_id_out), .data_in(data_in), .clk(Clk_out),
    .ld_sor(part3_state_table_1_ld_sor), .ld_end(part3_state_table_1_ld_end),
    .ld_reg(part3_state_table_1_ld_reg), .Reset(not_1_out), .ld_r(part3_state_table_1_id_r),
    .R_dend_val(part3_datapath_1_r_dend_val), .R_Reg_val(part3_datapath_1_r_reg_val),
    .R_sor_val(part3_datapath_1_r_sor_val), .remainder(part3_datapath_1_remainder),
    .quotient(part3_datapath_1_quotient));
  Hex_Digit_Display hex_digit_display_3 (.value(part3_datapath_1_r_dend_val[7:4]));  // open: dp
  Hex_Digit_Display hex_digit_display_4 (.value(part3_datapath_1_remainder[7:4]));  // open: dp
  Hex_Digit_Display hex_digit_display_5 (.value(part3_datapath_1_quotient[7:4]));  // open: dp
  Hex_Digit_Display hex_digit_display_6 (.value(part3_datapath_1_r_dend_val[3:0]));  // open: dp
  Hex_Digit_Display hex_digit_display_7 (.value(part3_datapath_1_r_reg_val[7:4]));  // open: dp
  Hex_Digit_Display hex_digit_display_8 (.value(part3_datapath_1_r_sor_val[7:4]));  // open: dp
  Hex_Digit_Display hex_digit_display_9 (.value(part3_datapath_1_r_sor_val[3:0]));  // open: dp
  Hex_Digit_Display hex_digit_display_10 (.value(part3_datapath_1_remainder[3:0]));  // open: dp
  Hex_Digit_Display hex_digit_display_11 (.value(part3_datapath_1_quotient[3:0]));  // open: dp
  Hex_Digit_Display hex_digit_display_12 (.value(part3_datapath_1_r_reg_val[3:0]));  // open: dp

  // Notes on the sheet:
  //   NOTE; divider is 5 digits maximum and dividend is 4digits maximum. 
endmodule
