// Logisim project lab7.circ as structural Verilog: 12 circuits, main circuit part1
module part1 (
  input  we,
  input  oe,
  input  reset,
  input  set_value_to_0,
  output [3:0] out_5
);

  wire clock_1_out;
  wire [3:0] adder_1_out, multiplexer_1_out, register_1_q;
  wire [4:0] adder_2_out, register_2_q;

  Adder #(.width(4)) adder_1 (.a(register_1_q), .b(4'b0001), .out(adder_1_out));  // open: cin, cout
  Clock clock_1 (.out(clock_1_out));
  Register #(.width(4)) register_1 (.D(adder_1_out), .en(1'b1), .clk(clock_1_out), .Q(register_1_q), .clr(reset));
  Adder #(.width(5)) adder_2 (.a(register_2_q), .b(5'b00001), .out(adder_2_out));  // open: cin, cout
  Register #(.width(5)) register_2 (.D(adder_2_out), .en(1'b1), .clk(clock_1_out), .Q(register_2_q), .clr(reset));
  Multiplexer #(.enable("false"), .width(4)) multiplexer_1 (
    .in0(register_1_q), .in1(4'b0000), .out(multiplexer_1_out), .sel(set_value_to_0));
  RAM #(.addrWidth(5), .dataWidth(4)) ram_1 (
    .addr(register_2_q), .we(we), .oe(oe), .clk(clock_1_out), .din(multiplexer_1_out), .dout(out_5));
  Hex_Digit_Display hex_digit_display_1 (.value(out_5));  // open: dp
endmodule

module part2 (
  input  [6:0] X,
  input  [6:0] Y,
  input  enable,
  input  reset,
  input  [23:0] color
);

  wire clock_1_out;
  wire [6:0] part2_submain_1_x_output, part2_submain_1_y_output;

  Clock clock_1 (.out(clock_1_out));
  part2_submain part2_submain_1 (
    .x(X), .y(Y), .clk(clock_1_out), .reset(reset), .x_output(part2_submain_1_x_output),
    .y_output(part2_submain_1_y_output));
  // RGB_Video rgb_video_1: pin names not known; wires that end beside it: reset, clock_1_out, enable, part2_submain_1_x_output, part2_submain_1_y_output, color, color
endmodule

module part3 (
  input  [6:0] X,
  input  [6:0] Y,
  input  enable,
  input  reset,
  input  [6:0] speed,
  input  [23:0] color
);

  wire clock_1_out, divideby256_1_counter_out, multiplexer_1_out;
  wire [6:0] part3_datapath_1_x_output, part3_datapath_1_y_output;

  Clock clock_1 (.out(clock_1_out));
  Multiplexer #(.enable("false")) multiplexer_1 (
    .in0(reset), .in1(divideby256_1_counter_out), .out(multiplexer_1_out), .sel(enable));
  divideBy256 divideby256_1 (.clear(reset), .clock(clock_1_out), .counter_out(divideby256_1_counter_out));
  part3_datapath part3_datapath_1 (
    .X(X), .Y(Y), .clk(clock_1_out), .reset(reset), .pixels(speed), .x_output(part3_datapath_1_x_output),
    .y_output(part3_datapath_1_y_output));
  // RGB_Video rgb_video_1: pin names not known; wires that end beside it: multiplexer_1_out, clock_1_out, enable, part3_datapath_1_x_output, part3_datapath_1_y_output, color
endmodule

module divideBy16 (
  input  clear,
  input  clock,
  output counter_out
);

  wire not_1_out, or_1_out;
  wire [3:0] counter_1_q;

  not not_1 (not_1_out, 1'b1);
  Counter #(.max('hf), .width(4)) counter_1 (
    .clr(clear), .load(or_1_out), .up(1'b1), .clk(clock), .D(4'b0000), .Q(counter_1_q));  // open: count, carry
  or or_1 (or_1_out, counter_out, not_1_out);
  and and_1 (counter_out, counter_1_q[0], counter_1_q[1], counter_1_q[2], counter_1_q[3]);
endmodule

module part2_submain (
  input  [6:0] x,
  input  [6:0] y,
  input  clk,
  input  reset,
  output [6:0] x_output,
  output [6:0] y_output
);

  wire [3:0] part2_fsm_1_connect_x, part2_fsm_1_connect_y;

  part2_fsm part2_fsm_1 (
    .clk(clk), .reset(reset), .connect_x(part2_fsm_1_connect_x), .connect_y(part2_fsm_1_connect_y));
  part2_datapath part2_datapath_1 (
    .X(x), .state_x(part2_fsm_1_connect_x), .Y(y), .state_y(part2_fsm_1_connect_y), .x_out(x_output),
    .y_out(y_output));
endmodule

module part2_datapath (
  input  [6:0] X,
  input  [3:0] state_x,
  input  [6:0] Y,
  input  [3:0] state_y,
  output [6:0] x_out,
  output [6:0] y_out
);

  wire [6:0] bit_extender_1_out, bit_extender_2_out;

  assign bit_extender_1_out = {{3{1'b0}}, state_x};  // Bit_Extender bit_extender_1
  assign bit_extender_2_out = {{3{1'b0}}, state_y};  // Bit_Extender bit_extender_2
  Adder #(.width(7)) adder_1 (.a(X), .b(bit_extender_1_out), .out(x_out));  // open: cin, cout
  Adder #(.width(7)) adder_2 (.a(bit_extender_2_out), .b(Y), .out(y_out));  // open: cin, cout
endmodule

module part2_fsm (
  input  clk,
  input  reset,
  output [3:0] connect_x,
  output [3:0] connect_y
);

  wire divideby16_1_counter_out;
  wire [3:0] adder_1_out, adder_2_out;

  Adder #(.width(4)) adder_1 (.a(connect_x), .b(4'b0001), .out(adder_1_out));  // open: cin, cout
  Register #(.width(4)) register_1 (.D(adder_1_out), .en(1'b1), .clk(clk), .Q(connect_x), .clr(reset));
  Adder #(.width(4)) adder_2 (.a(connect_y), .b(4'b0001), .out(adder_2_out));  // open: cin, cout
  Register #(.width(4)) register_2 (
    .D(adder_2_out), .en(divideby16_1_counter_out), .clk(clk), .Q(connect_y), .clr(reset));
  divideBy16 divideby16_1 (.clear(reset), .clock(clk), .counter_out(divideby16_1_counter_out));
endmodule

module part3_datapath (
  input  [6:0] X,
  input  [6:0] Y,
  input  clk,
  input  reset,
  input  [6:0] pixels,
  output [6:0] x_output,
  output [6:0] y_output
);

  wire divideby256_1_counter_out, keepatone_1_out_3, multiplexer_1_out;
  wire [1:0] changexy_1_next_dir, register_3_q;
  wire [6:0] changexy_1_next_x, changexy_1_next_y, multiplexer_2_out, multiplexer_3_out, register_1_q,
       register_2_q;

  Multiplexer #(.enable("false")) multiplexer_1 (
    .in0(1'b1), .in1(divideby256_1_counter_out), .out(multiplexer_1_out), .sel(keepatone_1_out_3));
  KeepAtOne keepatone_1 (.clear(reset), .clock(clk), .out_3(keepatone_1_out_3));
  Multiplexer #(.enable("false"), .width(7)) multiplexer_2 (
    .in0(X), .in1(changexy_1_next_x), .out(multiplexer_2_out), .sel(keepatone_1_out_3));
  Multiplexer #(.enable("false"), .width(7)) multiplexer_3 (
    .in0(Y), .in1(changexy_1_next_y), .out(multiplexer_3_out), .sel(keepatone_1_out_3));
  divideBy256 divideby256_1 (.clear(reset), .clock(clk), .counter_out(divideby256_1_counter_out));
  Register #(.width(7)) register_1 (
    .D(multiplexer_2_out), .en(multiplexer_1_out), .clk(clk), .Q(register_1_q), .clr(reset));
  Register #(.width(7)) register_2 (
    .D(multiplexer_3_out), .en(multiplexer_1_out), .clk(clk), .Q(register_2_q), .clr(reset));
  Register #(.width(2)) register_3 (
    .D(changexy_1_next_dir), .en(1'b1), .clk(divideby256_1_counter_out), .Q(register_3_q), .clr(reset));
  part2_submain part2_submain_1 (
    .x(register_1_q), .y(register_2_q), .clk(clk), .reset(reset), .x_output(x_output), .y_output(y_output));
  changexy changexy_1 (
    .pixels(pixels), .X(register_1_q), .y(register_2_q), .ori_dir(register_3_q), .next_x(changexy_1_next_x),
    .next_dir(changexy_1_next_dir), .next_y(changexy_1_next_y));
endmodule

module changexy (
  input  [6:0] pixels,
  input  [6:0] X,
  input  [6:0] y,
  input  [1:0] ori_dir,
  output [6:0] next_x,
  output [1:0] next_dir,
  output [6:0] next_y
);

  wire adder_3_cout, adder_5_cout, and_1_out, and_2_out, and_3_out, and_4_out, not_1_out, not_2_out,
       not_3_out, not_4_out, or_1_out, or_2_out, subtractor_1_bout, subtractor_2_bout;
  wire [6:0] adder_1_out, adder_2_out, adder_4_out, multiplexer_1_out, multiplexer_2_out, multiplexer_3_out,
       multiplexer_4_out, subtractor_1_out, subtractor_2_out;

  Adder #(.width(7)) adder_1 (.a(pixels), .b(7'b0010000), .out(adder_1_out));  // open: cin, cout
  Subtractor #(.width(7)) subtractor_1 (
    .a(X), .b(pixels), .out(subtractor_1_out), .bout(subtractor_1_bout));  // open: bin
  Adder #(.width(7)) adder_2 (.a(pixels), .b(X), .out(adder_2_out));  // open: cin, cout
  Adder #(.width(7)) adder_3 (.a(X), .b(adder_1_out), .cout(adder_3_cout));  // open: out, cin
  Adder #(.width(7)) adder_4 (.a(y), .b(pixels), .out(adder_4_out));  // open: cin, cout
  Subtractor #(.width(7)) subtractor_2 (
    .a(y), .b(pixels), .out(subtractor_2_out), .bout(subtractor_2_bout));  // open: bin
  Adder #(.width(7)) adder_5 (.a(y), .b(adder_1_out), .cout(adder_5_cout));  // open: out, cin
  Multiplexer #(.enable("false"), .width(7)) multiplexer_1 (
    .in0(adder_2_out), .in1(subtractor_1_out), .out(multiplexer_1_out), .sel(adder_3_cout));
  Multiplexer #(.enable("false"), .width(7)) multiplexer_2 (
    .in0(subtractor_1_out), .in1(adder_2_out), .out(multiplexer_2_out), .sel(subtractor_1_bout));
  Multiplexer #(.enable("false"), .width(7)) multiplexer_3 (
    .in0(adder_4_out), .in1(subtractor_2_out), .out(multiplexer_3_out), .sel(adder_5_cout));
  Multiplexer #(.enable("false"), .width(7)) multiplexer_4 (
    .in0(subtractor_2_out), .in1(adder_4_out), .out(multiplexer_4_out), .sel(subtractor_2_bout));
  not not_1 (not_1_out, ori_dir[0]);
  Multiplexer #(.enable("false"), .width(7)) multiplexer_5 (
    .in0(multiplexer_3_out), .in1(multiplexer_4_out), .out(next_y), .sel(ori_dir[1]));
  not not_2 (not_2_out, ori_dir[1]);
  Multiplexer #(.enable("false"), .width(7)) multiplexer_6 (
    .in0(multiplexer_2_out), .in1(multiplexer_1_out), .out(next_x), .sel(ori_dir[0]));
  and and_1 (and_1_out, ori_dir[0], adder_3_cout);
  and and_2 (and_2_out, not_1_out, subtractor_1_bout);
  and and_3 (and_3_out, ori_dir[1], subtractor_2_bout);
  and and_4 (and_4_out, not_2_out, adder_5_cout);
  not not_3 (not_3_out, ori_dir[0]);
  or or_1 (or_1_out, and_1_out, and_2_out);
  not not_4 (not_4_out, ori_dir[1]);
  or or_2 (or_2_out, and_3_out, and_4_out);
  Multiplexer #(.enable("false")) multiplexer_7 (.in0(ori_dir[0]), .in1(not_3_out), .out(next_dir[0]), .sel(or_1_out));
  Multiplexer #(.enable("false")) multiplexer_8 (.in0(ori_dir[1]), .in1(not_4_out), .out(next_dir[1]), .sel(or_2_out));

  // Notes on the sheet:
  //   original direction: go left
  //   original direction: go right
  //   original direction: go down
  //   original direction: go up
  //   00: down/left, 01: down/right, 10: up/left, 11: up/right
endmodule

module KeepAtOne (
  input  clear,
  input  clock,
  output out_3
);

  wire and_1_out, not_1_out, or_1_out;
  wire [0:0] counter_1_q;

  not not_1 (not_1_out, 1'b1);
  Counter #(.max('h2), .ongoal("stay"), .width(2)) counter_1 (
    .clr(clear), .load(or_1_out), .up(1'b1), .clk(clock), .D(2'b00), .Q({out_3, counter_1_q[0]}));  // open: count, carry
  or or_1 (or_1_out, and_1_out, not_1_out);
  and and_1 (and_1_out, counter_1_q[0], out_3);
endmodule

module divideBy2 (
  input  in_1,
  output out_2
);

  wire adder_1_out;

  Adder #(.width(1)) adder_1 (.a(out_2), .b(1'b1), .out(adder_1_out));  // open: cin, cout
  Register #(.width(1)) register_1 (.D(adder_1_out), .en(1'b1), .clk(in_1), .Q(out_2));  // open: clr
endmodule

module divideBy256 (
  input  clear,
  input  clock,
  output counter_out
);

  wire not_1_out, or_1_out;
  wire [7:0] counter_1_q;

  not not_1 (not_1_out, 1'b1);
  Counter counter_1 (
    .clr(clear), .load(or_1_out), .up(1'b1), .clk(clock), .D({8{1'b0}}), .Q(counter_1_q));  // open: count, carry
  or or_1 (or_1_out, counter_out, not_1_out);
  and and_1 (counter_out, counter_1_q[0], counter_1_q[1], counter_1_q[2], counter_1_q[3], counter_1_q[5], counter_1_q[6], counter_1_q[7], counter_1_q[4]);
endmodule
